// Logisim project nibbleOperator.circ as structural Verilog
module ALU (
  input  in_1,
  input  in_2,
  input  in_3,
  input  in_4,
  input  ZwR,
  input  SIn,
  input  RegIn,
  input  RSh,
  input  Sub,
  input  Inc,
  input  AddCF,
  input  CF,
  input  Op1,
  input  Op2,
  input  Op3,
  input  ZF,
  input  Out,
  input  Out_,
  output CF_2,
  output ZF_2,
  output out_21,
  output out_22,
  output out_23,
  output out_24
);

  wire and_1_out, and_2_out, and_3_out, and_4_out, and_5_out, and_6_out, and_7_out, and_8_out, and_9_out,
       and_10_out, and_11_out, and_12_out, and_13_out, and_14_out, and_15_out, and_16_out, and_17_out,
       and_18_out, and_19_out, and_20_out, and_21_out, and_22_out, and_23_out, and_24_out, and_25_out,
       and_26_out, and_27_out, and_28_out, and_29_out, controlled_buffer_4_out, d_ff_1_q, d_ff_2_q, d_ff_3_q,
       d_ff_4_q, d_ff_5_q, d_ff_6_q, d_ff_8_q, d_ff_9_q, or_1_out, or_2_out, or_3_out, or_4_out, or_5_out,
       or_6_out, or_7_out, or_8_out, or_9_out, or_10_out, or_11_out, or_12_out, or_13_out,
       undsteuerleitung_1_out_6, undsteuerleitung_1_out_7, undsteuerleitung_1_out_8,
       undsteuerleitung_1_out_9, undsteuerleitung_2_out_6, undsteuerleitung_2_out_7,
       undsteuerleitung_2_out_8, undsteuerleitung_2_out_9, undsteuerleitung_3_out_6,
       undsteuerleitung_3_out_7, undsteuerleitung_3_out_8, undsteuerleitung_3_out_9,
       undsteuerleitung_4_out_6, undsteuerleitung_4_out_7, undsteuerleitung_4_out_8,
       undsteuerleitung_4_out_9, undsteuerleitung_5_out_6, undsteuerleitung_5_out_7,
       undsteuerleitung_5_out_8, undsteuerleitung_5_out_9, volladdierer_1_out_4, volladdierer_1_out_5,
       volladdierer_2_out_4, volladdierer_2_out_5, volladdierer_3_out_4, volladdierer_3_out_5,
       volladdierer_4_out_4, volladdierer_4_out_5, xor_1_out, xor_2_out, xor_3_out, xor_4_out, xor_5_out,
       xor_6_out, xor_7_out, xor_8_out;

  xor xor_1 (xor_1_out, and_6_out, and_13_out);
  undSteuerleitung undsteuerleitung_1 (
    .in_1(xor_1_out), .in_2(xor_2_out), .in_3(xor_3_out), .in_4(xor_4_out), .Stleitung(and_1_out),
    .out_6(undsteuerleitung_1_out_6), .out_7(undsteuerleitung_1_out_7), .out_8(undsteuerleitung_1_out_8),
    .out_9(undsteuerleitung_1_out_9));
  xor xor_2 (xor_2_out, and_7_out, and_15_out);
  and and_1 (and_1_out, Op1, Op2, Op3);
  and and_2 (and_2_out, Op1, Op2, ~Op3);  // AND_Gate
  xor xor_3 (xor_3_out, and_8_out, and_16_out);
  xor xor_4 (xor_4_out, and_11_out, and_17_out);
  and and_3 (and_3_out, Op1, ~Op2, Op3);  // AND_Gate
  and and_4 (and_4_out, Op1, ~Op2, ~Op3);  // AND_Gate
  or or_1 (or_1_out, and_6_out, and_13_out);
  or or_2 (or_2_out, and_7_out, and_15_out);
  undSteuerleitung undsteuerleitung_2 (
    .in_1(or_1_out), .in_2(or_2_out), .in_3(or_4_out), .in_4(or_3_out), .Stleitung(and_2_out),
    .out_6(undsteuerleitung_2_out_6), .out_7(undsteuerleitung_2_out_7), .out_8(undsteuerleitung_2_out_8),
    .out_9(undsteuerleitung_2_out_9));
  and and_5 (and_5_out, ~Op1, Op2, Op3);  // AND_Gate
  D_Flip_Flop d_ff_1 (.clk(ZwR), .D(in_1), .Q(d_ff_1_q));  // open: Qn, preset, en, reset
  and and_6 (and_6_out, RegIn, d_ff_1_q);
  or or_3 (or_3_out, and_11_out, and_17_out);
  or or_4 (or_4_out, and_8_out, and_16_out);
  D_Flip_Flop d_ff_2 (.clk(ZwR), .D(in_2), .Q(d_ff_2_q));  // open: Qn, preset, en, reset
  and and_7 (and_7_out, RegIn, d_ff_2_q);
  D_Flip_Flop d_ff_3 (.clk(ZwR), .D(in_3), .Q(d_ff_3_q));  // open: Qn, preset, en, reset
  and and_8 (and_8_out, RegIn, d_ff_3_q);
  and and_9 (and_9_out, and_7_out, and_15_out);
  and and_10 (and_10_out, and_6_out, and_13_out);
  undSteuerleitung undsteuerleitung_3 (
    .in_1(and_10_out), .in_2(and_9_out), .in_3(and_12_out), .in_4(and_14_out), .Stleitung(and_3_out),
    .out_6(undsteuerleitung_3_out_6), .out_7(undsteuerleitung_3_out_7), .out_8(undsteuerleitung_3_out_8),
    .out_9(undsteuerleitung_3_out_9));
  or or_5 (or_5_out, undsteuerleitung_1_out_6, undsteuerleitung_2_out_6, undsteuerleitung_5_out_6, undsteuerleitung_3_out_6, undsteuerleitung_4_out_6);
  D_Flip_Flop d_ff_4 (.clk(ZwR), .D(in_4), .Q(d_ff_4_q));  // open: Qn, preset, en, reset
  and and_11 (and_11_out, RegIn, d_ff_4_q);
  and and_12 (and_12_out, and_8_out, and_16_out);
  or or_6 (or_6_out, undsteuerleitung_1_out_7, undsteuerleitung_2_out_7, undsteuerleitung_5_out_7, undsteuerleitung_3_out_7, undsteuerleitung_4_out_7);
  D_Flip_Flop d_ff_5 (.clk(Out), .D(or_5_out), .Q(d_ff_5_q));  // open: Qn, preset, en, reset
  assign out_21 = Out_ ? d_ff_5_q : 1'bz;  // Controlled_Buffer controlled_buffer_1
  and and_13 (and_13_out, in_1, SIn);
  and and_14 (and_14_out, and_11_out, and_17_out);
  or or_7 (or_7_out, undsteuerleitung_1_out_8, undsteuerleitung_2_out_8, undsteuerleitung_5_out_8, undsteuerleitung_3_out_8, undsteuerleitung_4_out_8);
  D_Flip_Flop d_ff_6 (.clk(Out), .D(or_6_out), .Q(d_ff_6_q));  // open: Qn, preset, en, reset
  assign out_22 = Out_ ? d_ff_6_q : 1'bz;  // Controlled_Buffer controlled_buffer_2
  and and_15 (and_15_out, in_2, SIn);
  and and_16 (and_16_out, in_3, SIn);
  D_Flip_Flop d_ff_7 (.clk(CF), .D(controlled_buffer_4_out), .Q(CF_2));  // open: Qn, preset, en, reset
  or or_8 (or_8_out, undsteuerleitung_1_out_9, undsteuerleitung_2_out_9, undsteuerleitung_5_out_9, undsteuerleitung_3_out_9, undsteuerleitung_4_out_9);
  D_Flip_Flop d_ff_8 (.clk(Out), .D(or_7_out), .Q(d_ff_8_q));  // open: Qn, preset, en, reset
  assign out_23 = Out_ ? d_ff_8_q : 1'bz;  // Controlled_Buffer controlled_buffer_3
  and and_17 (and_17_out, in_4, SIn);
  assign controlled_buffer_4_out = and_4_out ? volladdierer_2_out_5 : 1'bz;  // Controlled_Buffer controlled_buffer_4
  D_Flip_Flop d_ff_9 (.clk(Out), .D(or_8_out), .Q(d_ff_9_q));  // open: Qn, preset, en, reset
  assign out_24 = Out_ ? d_ff_9_q : 1'bz;  // Controlled_Buffer controlled_buffer_5
  xor xor_5 (xor_5_out, and_13_out, Sub);
  vollAddierer volladdierer_1 (
    .in_1(and_7_out), .in_2(xor_6_out), .in_3(volladdierer_3_out_5), .out_5(volladdierer_1_out_5),
    .out_4(volladdierer_1_out_4));
  vollAddierer volladdierer_2 (
    .in_1(and_6_out), .in_2(xor_5_out), .in_3(volladdierer_1_out_5), .out_5(volladdierer_2_out_5),
    .out_4(volladdierer_2_out_4));
  undSteuerleitung undsteuerleitung_4 (
    .in_1(volladdierer_2_out_4), .in_2(volladdierer_1_out_4), .in_3(volladdierer_3_out_4),
    .in_4(volladdierer_4_out_4), .Stleitung(and_4_out), .out_6(undsteuerleitung_4_out_6),
    .out_7(undsteuerleitung_4_out_7), .out_8(undsteuerleitung_4_out_8), .out_9(undsteuerleitung_4_out_9));
  and and_18 (and_18_out, ~or_5_out, ~or_6_out, ~or_7_out, ~or_8_out);  // AND_Gate
  xor xor_6 (xor_6_out, and_15_out, Sub);
  xor xor_7 (xor_7_out, and_16_out, Sub);
  vollAddierer volladdierer_3 (
    .in_1(and_8_out), .in_2(xor_7_out), .in_3(volladdierer_4_out_5), .out_5(volladdierer_3_out_5),
    .out_4(volladdierer_3_out_4));
  D_Flip_Flop d_ff_10 (.clk(ZF), .D(and_18_out), .Q(ZF_2));  // open: Qn, preset, en, reset
  xor xor_8 (xor_8_out, and_17_out, Sub);
  or or_9 (or_9_out, Inc, and_19_out);
  vollAddierer volladdierer_4 (
    .in_1(and_11_out), .in_2(xor_8_out), .in_3(or_9_out), .out_5(volladdierer_4_out_5),
    .out_4(volladdierer_4_out_4));
  and and_19 (and_19_out, AddCF, CF_2);
  and and_20 (and_20_out, and_13_out, ~RSh);  // AND_Gate
  and and_21 (and_21_out, and_5_out, ~RSh);  // AND_Gate
  assign controlled_buffer_4_out = and_21_out ? and_20_out : 1'bz;  // Controlled_Buffer controlled_buffer_6
  and and_22 (and_22_out, and_15_out, ~RSh);  // AND_Gate
  and and_23 (and_23_out, and_13_out, RSh);
  or or_10 (or_10_out, and_22_out, 1'b0);
  or or_11 (or_11_out, and_26_out, and_23_out);
  undSteuerleitung undsteuerleitung_5 (
    .in_1(or_10_out), .in_2(or_11_out), .in_3(or_12_out), .in_4(or_13_out), .Stleitung(and_5_out),
    .out_6(undsteuerleitung_5_out_6), .out_7(undsteuerleitung_5_out_7), .out_8(undsteuerleitung_5_out_8),
    .out_9(undsteuerleitung_5_out_9));
  and and_24 (and_24_out, and_16_out, RSh);
  and and_25 (and_25_out, and_15_out, RSh);
  and and_26 (and_26_out, and_16_out, ~RSh);  // AND_Gate
  or or_12 (or_12_out, and_27_out, and_25_out);
  and and_27 (and_27_out, and_17_out, ~RSh);  // AND_Gate
  and and_28 (and_28_out, and_17_out, RSh);
  assign controlled_buffer_4_out = and_29_out ? and_28_out : 1'bz;  // Controlled_Buffer controlled_buffer_7
  or or_13 (or_13_out, 1'b0, and_24_out);
  and and_29 (and_29_out, RSh, and_5_out);
endmodule

// undSt
module undSteuerleitung (
  input  in_1,
  input  in_2,
  input  in_3,
  input  in_4,
  input  Stleitung,
  output out_6,
  output out_7,
  output out_8,
  output out_9
);

  and and_1 (out_6, in_1, Stleitung);
  and and_2 (out_7, in_2, Stleitung);
  and and_3 (out_8, in_3, Stleitung);
  and and_4 (out_9, in_4, Stleitung);
endmodule

// VA
module vollAddierer (
  input  in_1,
  input  in_2,
  input  in_3,
  output out_4,
  output out_5
);

  wire and_1_out, and_2_out, and_3_out, and_4_out, xor_1_out, xor_2_out;

  and and_1 (and_1_out, in_1, in_2, in_3);
  and and_2 (and_2_out, in_1, in_2);
  ExactlyOne xor_1 (.out(xor_1_out), .in0(and_2_out), .in1(and_4_out), .in2(and_3_out));
  or or_1 (out_5, and_1_out, xor_1_out);
  and and_3 (and_3_out, in_2, in_3);
  and and_4 (and_4_out, in_1, in_3);
  or or_2 (out_4, and_1_out, xor_2_out);
  ExactlyOne xor_2 (.out(xor_2_out), .in0(in_1), .in1(in_2), .in2(in_3));
endmodule

module CPU (
  input  in_1,
  input  in_2,
  input  in_3,
  input  in_4,
  output out_5,
  output out_6,
  output out_7,
  output out_8,
  output out_9,
  output out_10,
  output out_11,
  output out_12,
  output out_13,
  output out_14,
  output out_15,
  output out_16
);

  wire addresswerk_1_out_24, addresswerk_1_out_25, addresswerk_1_out_26, addresswerk_1_out_27,
       addresswerk_1_out_28, addresswerk_1_out_29, addresswerk_1_out_30, addresswerk_1_out_31, alu_1_out_21;

  Addresswerk addresswerk_1 (
    .in_1(alu_1_out_21), .in_2(alu_1_out_21), .in_3(alu_1_out_21), .in_4(alu_1_out_21),
    .out_24(addresswerk_1_out_24), .out_25(addresswerk_1_out_25), .out_26(addresswerk_1_out_26),
    .out_27(addresswerk_1_out_27), .out_28(addresswerk_1_out_28), .out_29(addresswerk_1_out_29),
    .out_30(addresswerk_1_out_30), .out_31(addresswerk_1_out_31));  // open: CSIn, CSOut, IPExtIn, IPIn, IPInc, DSIn, DSOut, SIIn, ESIn, ESOut, DIIn, SSIn, BPIn, SSBPOut, SPExtIn, SPIn, SPInc, SPDec, SSSPOut
  ALU alu_1 (
    .in_1(alu_1_out_21), .in_2(alu_1_out_21), .in_3(alu_1_out_21), .in_4(alu_1_out_21),
    .out_21(alu_1_out_21), .out_22(alu_1_out_21), .out_23(alu_1_out_21), .out_24(alu_1_out_21));  // open: ZwR, SIn, RegIn, RSh, Sub, Inc, AddCF, CF, Op1, Op2, Op3, ZF, Out, Out_, CF_2, ZF_2
  Registersatz registersatz_1 (
    .in_2(alu_1_out_21), .in_3(alu_1_out_21), .in_4(alu_1_out_21), .in_5(alu_1_out_21),
    .out_10(alu_1_out_21), .out_11(alu_1_out_21), .out_12(alu_1_out_21), .out_13(alu_1_out_21));  // open: In, Out, in_7, in_8, in_9
  BIU biu_1 (
    .out_25(alu_1_out_21), .out_26(alu_1_out_21), .out_27(alu_1_out_21), .out_28(alu_1_out_21),
    .in_1(alu_1_out_21), .in_2(alu_1_out_21), .in_3(alu_1_out_21), .in_4(alu_1_out_21),
    .in_5(addresswerk_1_out_24), .in_6(addresswerk_1_out_25), .in_7(addresswerk_1_out_26),
    .in_8(addresswerk_1_out_27), .in_9(addresswerk_1_out_28), .in_10(addresswerk_1_out_29),
    .in_11(addresswerk_1_out_30), .in_12(addresswerk_1_out_31), .out_29(out_16), .out_30(out_15),
    .out_31(out_14), .out_32(out_13), .in_18(in_4), .in_19(in_3), .in_20(in_2), .in_21(in_1),
    .out_33(out_12), .out_34(out_11), .out_35(out_10), .out_36(out_9), .out_37(out_8), .out_38(out_7),
    .out_39(out_6), .out_40(out_5));  // open: in_13, in_14, in_15, in_16, in_17, in_22, in_23, in_24
endmodule

module Registersatz (
  input  In,
  input  in_2,
  input  in_3,
  input  in_4,
  input  in_5,
  input  Out,
  input  in_7,
  input  in_8,
  input  in_9,
  output out_10,
  output out_11,
  output out_12,
  output out_13
);

  wire and_1_out, and_2_out, and_3_out, and_4_out, and_5_out, and_6_out, and_7_out, and_8_out,
       undinout_1_out_4, undinout_1_out_5, undinout_2_out_4, undinout_2_out_5, undinout_3_out_4,
       undinout_3_out_5, undinout_4_out_4, undinout_4_out_5, undinout_5_out_4, undinout_5_out_5,
       undinout_6_out_4, undinout_6_out_5, undinout_7_out_4, undinout_7_out_5, undinout_8_out_4,
       undinout_8_out_5;

  and and_1 (and_1_out, in_7, in_8, in_9);
  and and_2 (and_2_out, in_7, in_8, ~in_9);  // AND_Gate
  and and_3 (and_3_out, in_7, ~in_8, in_9);  // AND_Gate
  and and_4 (and_4_out, in_7, ~in_8, ~in_9);  // AND_Gate
  and and_5 (and_5_out, ~in_7, in_8, in_9);  // AND_Gate
  and and_6 (and_6_out, ~in_7, in_8, ~in_9);  // AND_Gate
  and and_7 (and_7_out, ~in_7, ~in_8, in_9);  // AND_Gate
  and and_8 (and_8_out, ~in_7, ~in_8, ~in_9);  // AND_Gate
  undInOut undinout_1 (.in_2(In), .in_3(Out), .in_1(and_1_out), .out_4(undinout_1_out_4), .out_5(undinout_1_out_5));
  Register AX (
    .RegIn(undinout_1_out_4), .RegOut(undinout_1_out_5), .MSB(in_2), .in_2(in_3), .in_3(in_4), .LSB(in_5),
    .out_7(out_10), .out_8(out_11), .out_9(out_12), .out_10(out_13));
  Register BX (
    .RegIn(undinout_2_out_4), .RegOut(undinout_2_out_5), .MSB(in_2), .in_2(in_3), .in_3(in_4), .LSB(in_5),
    .out_7(out_10), .out_8(out_11), .out_9(out_12), .out_10(out_13));
  undInOut undinout_2 (.in_2(In), .in_3(Out), .in_1(and_2_out), .out_4(undinout_2_out_4), .out_5(undinout_2_out_5));
  Register CX (
    .RegIn(undinout_3_out_4), .RegOut(undinout_3_out_5), .MSB(in_2), .in_2(in_3), .in_3(in_4), .LSB(in_5),
    .out_7(out_10), .out_8(out_11), .out_9(out_12), .out_10(out_13));
  undInOut undinout_3 (.in_2(In), .in_3(Out), .in_1(and_3_out), .out_4(undinout_3_out_4), .out_5(undinout_3_out_5));
  Register DX (
    .RegIn(undinout_4_out_4), .RegOut(undinout_4_out_5), .MSB(in_2), .in_2(in_3), .in_3(in_4), .LSB(in_5),
    .out_7(out_10), .out_8(out_11), .out_9(out_12), .out_10(out_13));
  undInOut undinout_4 (.in_2(In), .in_3(Out), .in_1(and_4_out), .out_4(undinout_4_out_4), .out_5(undinout_4_out_5));
  undInOut undinout_5 (.in_2(In), .in_3(Out), .in_1(and_5_out), .out_4(undinout_5_out_4), .out_5(undinout_5_out_5));
  Register EX (
    .RegIn(undinout_5_out_4), .RegOut(undinout_5_out_5), .MSB(in_2), .in_2(in_3), .in_3(in_4), .LSB(in_5),
    .out_7(out_10), .out_8(out_11), .out_9(out_12), .out_10(out_13));
  Register FX (
    .RegIn(undinout_6_out_4), .RegOut(undinout_6_out_5), .MSB(in_2), .in_2(in_3), .in_3(in_4), .LSB(in_5),
    .out_7(out_10), .out_8(out_11), .out_9(out_12), .out_10(out_13));
  undInOut undinout_6 (.in_2(In), .in_3(Out), .in_1(and_6_out), .out_4(undinout_6_out_4), .out_5(undinout_6_out_5));
  Register GX (
    .RegIn(undinout_7_out_4), .RegOut(undinout_7_out_5), .MSB(in_2), .in_2(in_3), .in_3(in_4), .LSB(in_5),
    .out_7(out_10), .out_8(out_11), .out_9(out_12), .out_10(out_13));
  undInOut undinout_7 (.in_2(In), .in_3(Out), .in_1(and_7_out), .out_4(undinout_7_out_4), .out_5(undinout_7_out_5));
  Register HX (
    .RegIn(undinout_8_out_4), .RegOut(undinout_8_out_5), .MSB(in_2), .in_2(in_3), .in_3(in_4), .LSB(in_5),
    .out_7(out_10), .out_8(out_11), .out_9(out_12), .out_10(out_13));
  undInOut undinout_8 (.in_2(In), .in_3(Out), .in_1(and_8_out), .out_4(undinout_8_out_4), .out_5(undinout_8_out_5));
endmodule

// Reg
module Register (
  input  MSB,
  input  in_2,
  input  in_3,
  input  LSB,
  input  RegIn,
  input  RegOut,
  output out_7,
  output out_8,
  output out_9,
  output out_10
);

  wire d_ff_1_q, d_ff_2_q, d_ff_3_q, d_ff_4_q;

  D_Flip_Flop d_ff_1 (.clk(RegIn), .D(MSB), .Q(d_ff_1_q));  // open: Qn, preset, en, reset
  assign out_7 = RegOut ? d_ff_1_q : 1'bz;  // Controlled_Buffer controlled_buffer_1
  D_Flip_Flop d_ff_2 (.clk(RegIn), .D(in_2), .Q(d_ff_2_q));  // open: Qn, preset, en, reset
  assign out_8 = RegOut ? d_ff_2_q : 1'bz;  // Controlled_Buffer controlled_buffer_2
  D_Flip_Flop d_ff_3 (.clk(RegIn), .D(in_3), .Q(d_ff_3_q));  // open: Qn, preset, en, reset
  assign out_9 = RegOut ? d_ff_3_q : 1'bz;  // Controlled_Buffer controlled_buffer_3
  D_Flip_Flop d_ff_4 (.clk(RegIn), .D(LSB), .Q(d_ff_4_q));  // open: Qn, preset, en, reset
  assign out_10 = RegOut ? d_ff_4_q : 1'bz;  // Controlled_Buffer controlled_buffer_4
endmodule

// uInOut
module undInOut (
  input  in_1,
  input  in_2,
  input  in_3,
  output out_4,
  output out_5
);

  and and_1 (out_4, in_1, in_2);
  and and_2 (out_5, in_1, in_3);
endmodule

module Addresswerk (
  input  in_1,
  input  in_2,
  input  in_3,
  input  in_4,
  input  CSIn,
  input  CSOut,
  input  IPExtIn,
  input  IPIn,
  input  IPInc,
  input  DSIn,
  input  DSOut,
  input  SIIn,
  input  ESIn,
  input  ESOut,
  input  DIIn,
  input  SSIn,
  input  BPIn,
  input  SSBPOut,
  input  SPExtIn,
  input  SPIn,
  input  SPInc,
  input  SPDec,
  input  SSSPOut,
  output out_24,
  output out_25,
  output out_26,
  output out_27,
  output out_28,
  output out_29,
  output out_30,
  output out_31
);

  wire or_1_out;

  or or_1 (or_1_out, SSBPOut, SSSPOut);
  Register CS (
    .RegIn(CSIn), .RegOut(CSOut), .MSB(in_1), .in_2(in_2), .in_3(in_3), .LSB(in_4), .out_7(out_24),
    .out_8(out_25), .out_9(out_26), .out_10(out_27));
  Register ES (
    .RegIn(ESIn), .RegOut(ESOut), .MSB(in_1), .in_2(in_2), .in_3(in_3), .LSB(in_4), .out_7(out_24),
    .out_8(out_25), .out_9(out_26), .out_10(out_27));
  InstructionPointer instructionpointer_1 (
    .ExtIn(IPExtIn), .In(IPIn), .Out(CSOut), .IncIn(IPInc), .in_1(in_1), .in_2(in_2), .in_3(in_3),
    .in_4(in_4), .out_9(out_28), .out_10(out_29), .out_11(out_30), .out_12(out_31));
  Register DI (
    .RegIn(DIIn), .RegOut(ESOut), .MSB(in_1), .in_2(in_2), .in_3(in_3), .LSB(in_4), .out_7(out_31),
    .out_8(out_30), .out_9(out_29), .out_10(out_28));
  Register DS (
    .RegIn(DSIn), .RegOut(DSOut), .MSB(in_1), .in_2(in_2), .in_3(in_3), .LSB(in_4), .out_7(out_24),
    .out_8(out_25), .out_9(out_26), .out_10(out_27));
  Register SS (
    .RegIn(SSIn), .RegOut(or_1_out), .MSB(in_1), .in_2(in_2), .in_3(in_3), .LSB(in_4), .out_7(out_24),
    .out_8(out_25), .out_9(out_26), .out_10(out_27));
  Register SI (
    .RegIn(SIIn), .RegOut(DSOut), .MSB(in_1), .in_2(in_2), .in_3(in_3), .LSB(in_4), .out_7(out_28),
    .out_8(out_29), .out_9(out_30), .out_10(out_31));
  Register BP (
    .RegIn(BPIn), .RegOut(SSBPOut), .MSB(in_1), .in_2(in_2), .in_3(in_3), .LSB(in_4), .out_7(out_31),
    .out_8(out_30), .out_9(out_29), .out_10(out_28));
  StackPointer stackpointer_1 (
    .ExtIn(SPExtIn), .In(SPIn), .IncIn(SPInc), .DecIn(SPDec), .Out(SSSPOut), .in_1(in_1), .in_2(in_2),
    .in_3(in_3), .in_4(in_4), .out_10(out_28), .out_11(out_29), .out_12(out_30), .out_13(out_31));
endmodule

// IP
module InstructionPointer (
  input  in_1,
  input  in_2,
  input  in_3,
  input  in_4,
  input  ExtIn,
  input  In,
  input  Out,
  input  IncIn,
  output out_9,
  output out_10,
  output out_11,
  output out_12
);

  wire controlled_buffer_1_out, controlled_buffer_2_out, controlled_buffer_3_out, controlled_buffer_6_out,
       d_ff_1_q, d_ff_2_q, d_ff_3_q, d_ff_4_q, halbaddierer_1_out_4, halbaddierer_2_out_3,
       halbaddierer_2_out_4, halbaddierer_3_out_3, halbaddierer_3_out_4, halbaddierer_4_out_3,
       halbaddierer_4_out_4;

  assign controlled_buffer_1_out = ExtIn ? in_1 : 1'bz;  // Controlled_Buffer controlled_buffer_1
  halbAddierer halbaddierer_1 (
    .in_1(d_ff_1_q), .in_2(halbaddierer_2_out_3), .out_4(halbaddierer_1_out_4));  // open: out_3
  assign controlled_buffer_2_out = ExtIn ? in_3 : 1'bz;  // Controlled_Buffer controlled_buffer_2
  assign controlled_buffer_3_out = ExtIn ? in_2 : 1'bz;  // Controlled_Buffer controlled_buffer_3
  D_Flip_Flop d_ff_1 (.clk(In), .D(controlled_buffer_1_out), .Q(d_ff_1_q));  // open: Qn, preset, en, reset
  halbAddierer halbaddierer_2 (
    .in_1(d_ff_2_q), .in_2(halbaddierer_3_out_3), .out_3(halbaddierer_2_out_3), .out_4(halbaddierer_2_out_4));
  assign controlled_buffer_1_out = IncIn ? halbaddierer_1_out_4 : 1'bz;  // Controlled_Buffer controlled_buffer_4
  assign controlled_buffer_3_out = IncIn ? halbaddierer_2_out_4 : 1'bz;  // Controlled_Buffer controlled_buffer_5
  assign controlled_buffer_6_out = ExtIn ? in_4 : 1'bz;  // Controlled_Buffer controlled_buffer_6
  D_Flip_Flop d_ff_2 (.clk(In), .D(controlled_buffer_3_out), .Q(d_ff_2_q));  // open: Qn, preset, en, reset
  halbAddierer halbaddierer_3 (
    .in_1(d_ff_3_q), .in_2(halbaddierer_4_out_3), .out_3(halbaddierer_3_out_3), .out_4(halbaddierer_3_out_4));
  halbAddierer halbaddierer_4 (
    .in_1(d_ff_4_q), .in_2(1'b1), .out_3(halbaddierer_4_out_3), .out_4(halbaddierer_4_out_4));
  assign controlled_buffer_2_out = IncIn ? halbaddierer_3_out_4 : 1'bz;  // Controlled_Buffer controlled_buffer_7
  assign controlled_buffer_6_out = IncIn ? halbaddierer_4_out_4 : 1'bz;  // Controlled_Buffer controlled_buffer_8
  D_Flip_Flop d_ff_3 (.clk(In), .D(controlled_buffer_2_out), .Q(d_ff_3_q));  // open: Qn, preset, en, reset
  assign out_9 = Out ? d_ff_1_q : 1'bz;  // Controlled_Buffer controlled_buffer_9
  assign out_10 = Out ? d_ff_2_q : 1'bz;  // Controlled_Buffer controlled_buffer_10
  D_Flip_Flop d_ff_4 (.clk(In), .D(controlled_buffer_6_out), .Q(d_ff_4_q));  // open: Qn, preset, en, reset
  assign out_11 = Out ? d_ff_3_q : 1'bz;  // Controlled_Buffer controlled_buffer_11
  assign out_12 = Out ? d_ff_4_q : 1'bz;  // Controlled_Buffer controlled_buffer_12
endmodule

// HA
module halbAddierer (
  input  in_1,
  input  in_2,
  output out_3,
  output out_4
);

  and and_1 (out_3, in_1, in_2);
  xor xor_1 (out_4, in_1, in_2);
endmodule

// SP
module StackPointer (
  input  in_1,
  input  in_2,
  input  in_3,
  input  in_4,
  input  ExtIn,
  input  In,
  input  IncIn,
  input  DecIn,
  input  Out,
  output out_10,
  output out_11,
  output out_12,
  output out_13
);

  wire controlled_buffer_1_out, controlled_buffer_2_out, controlled_buffer_3_out, controlled_buffer_6_out,
       d_ff_1_q, d_ff_2_q, d_ff_3_q, d_ff_4_q, halbaddierer_1_out_4, halbaddierer_2_out_3,
       halbaddierer_2_out_4, halbaddierer_3_out_3, halbaddierer_3_out_4, halbaddierer_4_out_3,
       halbaddierer_4_out_4, halbaddierer_5_out_3, halbaddierer_5_out_4, volladdierer_1_out_4,
       volladdierer_2_out_4, volladdierer_2_out_5, volladdierer_3_out_4, volladdierer_3_out_5;

  assign controlled_buffer_1_out = ExtIn ? in_1 : 1'bz;  // Controlled_Buffer controlled_buffer_1
  halbAddierer halbaddierer_1 (
    .in_1(d_ff_1_q), .in_2(halbaddierer_2_out_3), .out_4(halbaddierer_1_out_4));  // open: out_3
  assign controlled_buffer_2_out = ExtIn ? in_3 : 1'bz;  // Controlled_Buffer controlled_buffer_2
  assign controlled_buffer_3_out = ExtIn ? in_2 : 1'bz;  // Controlled_Buffer controlled_buffer_3
  D_Flip_Flop d_ff_1 (.clk(In), .D(controlled_buffer_1_out), .Q(d_ff_1_q));  // open: Qn, preset, en, reset
  halbAddierer halbaddierer_2 (
    .in_1(d_ff_2_q), .in_2(halbaddierer_3_out_3), .out_3(halbaddierer_2_out_3), .out_4(halbaddierer_2_out_4));
  assign controlled_buffer_1_out = IncIn ? halbaddierer_1_out_4 : 1'bz;  // Controlled_Buffer controlled_buffer_4
  assign controlled_buffer_3_out = IncIn ? halbaddierer_2_out_4 : 1'bz;  // Controlled_Buffer controlled_buffer_5
  assign controlled_buffer_6_out = ExtIn ? in_4 : 1'bz;  // Controlled_Buffer controlled_buffer_6
  D_Flip_Flop d_ff_2 (.clk(In), .D(controlled_buffer_3_out), .Q(d_ff_2_q));  // open: Qn, preset, en, reset
  halbAddierer halbaddierer_3 (
    .in_1(d_ff_3_q), .in_2(halbaddierer_4_out_3), .out_3(halbaddierer_3_out_3), .out_4(halbaddierer_3_out_4));
  halbAddierer halbaddierer_4 (
    .in_1(d_ff_4_q), .in_2(1'b1), .out_3(halbaddierer_4_out_3), .out_4(halbaddierer_4_out_4));
  assign controlled_buffer_6_out = IncIn ? halbaddierer_4_out_4 : 1'bz;  // Controlled_Buffer controlled_buffer_7
  assign controlled_buffer_2_out = IncIn ? halbaddierer_3_out_4 : 1'bz;  // Controlled_Buffer controlled_buffer_8
  D_Flip_Flop d_ff_3 (.clk(In), .D(controlled_buffer_2_out), .Q(d_ff_3_q));  // open: Qn, preset, en, reset
  vollAddierer volladdierer_1 (
    .in_1(d_ff_1_q), .in_2(1'b1), .in_3(volladdierer_3_out_5), .out_4(volladdierer_1_out_4));  // open: out_5
  assign controlled_buffer_1_out = DecIn ? volladdierer_1_out_4 : 1'bz;  // Controlled_Buffer controlled_buffer_9
  D_Flip_Flop d_ff_4 (.clk(In), .D(controlled_buffer_6_out), .Q(d_ff_4_q));  // open: Qn, preset, en, reset
  vollAddierer volladdierer_2 (
    .in_1(d_ff_3_q), .in_2(1'b1), .in_3(halbaddierer_5_out_3), .out_5(volladdierer_2_out_5),
    .out_4(volladdierer_2_out_4));
  vollAddierer volladdierer_3 (
    .in_1(d_ff_2_q), .in_2(1'b1), .in_3(volladdierer_2_out_5), .out_5(volladdierer_3_out_5),
    .out_4(volladdierer_3_out_4));
  assign controlled_buffer_3_out = DecIn ? volladdierer_3_out_4 : 1'bz;  // Controlled_Buffer controlled_buffer_10
  assign controlled_buffer_2_out = DecIn ? volladdierer_2_out_4 : 1'bz;  // Controlled_Buffer controlled_buffer_11
  halbAddierer halbaddierer_5 (
    .in_1(d_ff_4_q), .in_2(1'b1), .out_3(halbaddierer_5_out_3), .out_4(halbaddierer_5_out_4));
  assign controlled_buffer_6_out = DecIn ? halbaddierer_5_out_4 : 1'bz;  // Controlled_Buffer controlled_buffer_12
  assign out_10 = Out ? d_ff_1_q : 1'bz;  // Controlled_Buffer controlled_buffer_13
  assign out_11 = Out ? d_ff_2_q : 1'bz;  // Controlled_Buffer controlled_buffer_14
  assign out_13 = Out ? d_ff_4_q : 1'bz;  // Controlled_Buffer controlled_buffer_15
  assign out_12 = Out ? d_ff_3_q : 1'bz;  // Controlled_Buffer controlled_buffer_16
endmodule

module BIU (
  input  in_1,
  input  in_2,
  input  in_3,
  input  in_4,
  input  in_5,
  input  in_6,
  input  in_7,
  input  in_8,
  input  in_9,
  input  in_10,
  input  in_11,
  input  in_12,
  input  in_13,
  input  in_14,
  input  in_15,
  input  in_16,
  input  in_17,
  input  in_18,
  input  in_19,
  input  in_20,
  input  in_21,
  input  in_22,
  input  in_23,
  input  in_24,
  output out_25,
  output out_26,
  output out_27,
  output out_28,
  output out_29,
  output out_30,
  output out_31,
  output out_32,
  output out_33,
  output out_34,
  output out_35,
  output out_36,
  output out_37,
  output out_38,
  output out_39,
  output out_40
);

  Datenbustreiber datenbustreiber_1 (
    .In(in_13), .G(in_14), .Dir(in_15), .Out1(in_16), .Out2(in_17), .out_14(out_25), .out_15(out_26),
    .out_16(out_27), .out_17(out_28), .in_1(in_1), .in_2(in_2), .in_3(in_3), .in_4(in_4), .out_18(out_29),
    .out_19(out_30), .out_20(out_31), .out_21(out_32), .in_10(in_18), .in_11(in_19), .in_12(in_20),
    .in_13(in_21));
  Addressbustreiber addressbustreiber_1 (
    .In(in_22), .G(in_23), .Out1(in_24), .in_1(in_5), .in_2(in_6), .in_3(in_7), .in_4(in_8), .in_5(in_9),
    .in_6(in_10), .in_7(in_11), .in_8(in_12), .out_12(out_33), .out_13(out_34), .out_14(out_35),
    .out_15(out_36), .out_16(out_37), .out_17(out_38), .out_18(out_39), .out_19(out_40));
endmodule

module Datenbustreiber (
  input  in_1,
  input  in_2,
  input  in_3,
  input  in_4,
  input  In,
  input  G,
  input  Dir,
  input  Out1,
  input  Out2,
  input  in_10,
  input  in_11,
  input  in_12,
  input  in_13,
  output out_14,
  output out_15,
  output out_16,
  output out_17,
  output out_18,
  output out_19,
  output out_20,
  output out_21
);

  BidirektionalesSpeicherding bidirektionalesspeicherding_1 (
    .In(In), .G(G), .Dir(Dir), .Out1(Out1), .Out2(Out2), .out_8(out_14), .in_2(in_1), .out_9(out_18),
    .in_7(in_10));
  BidirektionalesSpeicherding bidirektionalesspeicherding_2 (
    .In(In), .G(G), .Dir(Dir), .Out1(Out1), .Out2(Out2), .out_8(out_15), .in_2(in_2), .out_9(out_19),
    .in_7(in_11));
  BidirektionalesSpeicherding bidirektionalesspeicherding_3 (
    .In(In), .G(G), .Dir(Dir), .Out1(Out1), .Out2(Out2), .out_8(out_16), .in_2(in_3), .out_9(out_20),
    .in_7(in_12));
  BidirektionalesSpeicherding bidirektionalesspeicherding_4 (
    .In(In), .G(G), .Dir(Dir), .Out1(Out1), .Out2(Out2), .out_8(out_17), .in_2(in_4), .out_9(out_21),
    .in_7(in_13));
endmodule

// DI
module BidirektionalesSpeicherding (
  input  In,
  input  in_2,
  input  G,
  input  Dir,
  input  Out1,
  input  Out2,
  input  in_7,
  output out_8,
  output out_9
);

  wire and_1_out, and_2_out, and_3_out, and_4_out, controlled_buffer_2_out, d_ff_1_q;

  and and_1 (and_1_out, G, Dir);
  and and_2 (and_2_out, G, ~Dir);  // AND_Gate
  assign out_8 = and_3_out ? d_ff_1_q : 1'bz;  // Controlled_Buffer controlled_buffer_1
  and and_3 (and_3_out, Out1, and_1_out);
  assign controlled_buffer_2_out = and_1_out ? in_2 : 1'bz;  // Controlled_Buffer controlled_buffer_2
  D_Flip_Flop d_ff_1 (.clk(In), .D(controlled_buffer_2_out), .Q(d_ff_1_q));  // open: Qn, preset, en, reset
  assign controlled_buffer_2_out = and_2_out ? in_7 : 1'bz;  // Controlled_Buffer controlled_buffer_3
  and and_4 (and_4_out, and_2_out, Out2);
  assign out_9 = and_4_out ? d_ff_1_q : 1'bz;  // Controlled_Buffer controlled_buffer_4
endmodule

module Addressbustreiber (
  input  in_1,
  input  in_2,
  input  in_3,
  input  in_4,
  input  in_5,
  input  in_6,
  input  in_7,
  input  in_8,
  input  In,
  input  G,
  input  Out1,
  output out_12,
  output out_13,
  output out_14,
  output out_15,
  output out_16,
  output out_17,
  output out_18,
  output out_19
);

  UnidirektionalesSpeicherDing unidirektionalesspeicherding_1 (
    .In(In), .G(G), .Out1(Out1), .in_2(in_1), .out_5(out_12));
  UnidirektionalesSpeicherDing unidirektionalesspeicherding_2 (
    .In(In), .G(G), .Out1(Out1), .in_2(in_2), .out_5(out_13));
  UnidirektionalesSpeicherDing unidirektionalesspeicherding_3 (
    .In(In), .G(G), .Out1(Out1), .in_2(in_3), .out_5(out_14));
  UnidirektionalesSpeicherDing unidirektionalesspeicherding_4 (
    .In(In), .G(G), .Out1(Out1), .in_2(in_4), .out_5(out_15));
  UnidirektionalesSpeicherDing unidirektionalesspeicherding_5 (
    .In(In), .G(G), .Out1(Out1), .in_2(in_5), .out_5(out_16));
  UnidirektionalesSpeicherDing unidirektionalesspeicherding_6 (.In(In), .in_2(in_6), .out_5(out_17));  // open: G, Out1
  UnidirektionalesSpeicherDing unidirektionalesspeicherding_7 (
    .In(In), .G(G), .Out1(Out1), .in_2(in_7), .out_5(out_18));
  UnidirektionalesSpeicherDing unidirektionalesspeicherding_8 (
    .In(In), .G(G), .Out1(Out1), .in_2(in_8), .out_5(out_19));
endmodule

// AI
module UnidirektionalesSpeicherDing (
  input  In,
  input  in_2,
  input  G,
  input  Out1,
  output out_5
);

  wire and_1_out, controlled_buffer_1_out, d_ff_1_q;

  assign controlled_buffer_1_out = G ? in_2 : 1'bz;  // Controlled_Buffer controlled_buffer_1
  D_Flip_Flop d_ff_1 (.clk(In), .D(controlled_buffer_1_out), .Q(d_ff_1_q));  // open: Qn, preset, en, reset
  and and_1 (and_1_out, Out1, G);
  assign out_5 = and_1_out ? d_ff_1_q : 1'bz;  // Controlled_Buffer controlled_buffer_2
endmodule
